# Fritzing sketch 7805+Zener (saved by Fritzing 0.9.0b)
breadboards: 1

parts:
  U1 = Voltage Regulator - 5V [package="TO220 [THT]"]
  VCC1 = Battery block 9V
  VCC2 = Battery block 9V
  C1 = Electrolytic Capacitor [capacitance=10µF package="100 mil [THT, electrolytic]"]
  C2 = Ceramic Capacitor [capacitance=100nF package="100 mil [THT, multilayer]"]
  C3 = Electrolytic Capacitor [capacitance=1µF package="100 mil [THT, electrolytic]"]
  R4 = Resistor [tolerance=±5% resistance=220 package=THT]
  D1 = Zener Diode [part_number=1N4732A breakdown_voltage=3.6V package="300 mil [THT]"]
  C4 = Ceramic Capacitor [capacitance=100nF package="100 mil [THT, multilayer]"]
  D2 = Schottky Diode [part_number=1N5817 package="Melf DO-213 AB [SMD]"]
  R5 = Resistor [tolerance=±5% resistance=330 package=THT]
  R6 = Resistor [tolerance=±5% resistance=220 package=THT]
  Q1 = PNP-Transistor [package="TO92 [THT]"]
  C5 = Ceramic Capacitor [capacitance=100nF package="100 mil [THT, multilayer]"]
  R7 = Resistor [tolerance=±5% resistance=220 package=THT]
  D3 = Zener Diode [part_number=1N4732A breakdown_voltage=3.6V package="300 mil [THT]"]

nets:
  N1: U1.input_voltage, VCC1.+, C1.+, C2.1, D2.cathode
  N2: U1.GND, R6.Pin_1, Q1.E
  N3: U1.output_voltage, C3.+, R4.Pin_0, C4.0, D2.anode, R6.Pin_0
  N4: VCC1.-, VCC2.+, C5.1, D3.cathode
  N5: VCC2.-, Q1.B, R7.Pin_1
  N6: C1.-, C2.0
  N7: C3.-, D1.anode, C4.1, R5.Pin_0
  N8: R4.Pin_1, D1.cathode, R5.Pin_1
  N9: Q1.C, C5.0, R7.Pin_0, D3.anode

notes:
  10.5V
  負電源
  GND
  GND
  正電源
