# Fritzing sketch Arduino-I2C-Level-Shift-LED-LCD (saved by Fritzing 0.9.0b)
breadboards: 1

parts:
  U1 = mystery part, 5 pins [chip_label="I2C LCD"]
  パーツ1 = Arduino Uno (Rev3)
  R1 = Resistor [tolerance=±5% resistance=10k package=THT]
  R2 = Resistor [tolerance=±5% resistance=330 package=THT]
  R3 = Resistor [tolerance=±5% resistance=330 package=THT]
  LED1 = LED - 3mm [color="Blue (525nm)" package="3 mm [THT]"]
  R4 = Resistor [tolerance=±5% resistance=10k package=THT]
  R5 = Resistor [tolerance=±5% resistance=10k package=THT]
  R6 = Resistor [tolerance=±5% resistance=330 package=THT]
  R7 = Resistor [tolerance=±5% resistance=330 package=THT]
  LED2 = LED - 3mm [color="Blue (525nm)" package="3 mm [THT]"]
  R8 = Resistor [tolerance=±5% resistance=10k package=THT]
  LED3 = LED - 3mm [color="Blue (525nm)" package="3 mm [THT]"]
  R9 = Resistor [tolerance=±5% resistance=10k package=THT]
  R10 = Resistor [tolerance=±5% resistance=330 package=THT]
  R11 = Resistor [tolerance=±5% resistance=330 package=THT]
  R12 = Resistor [tolerance=±5% resistance=10k package=THT]
  J1 = female pin header, 1 pin [form="♀ (female)"]
  J2 = female pin header, 1 pin [form="♀ (female)"]
  J3 = female pin header, 1 pin [form="♀ (female)"]

nets:
  N1: U1.pin1, パーツ1.3V3, R1.Pin_1, R5.Pin_1, R9.Pin_1
  N2: U1.pin2, R1.Pin_0, R2.Pin_0, J1.pin1
  N3: U1.pin3, R5.Pin_0, R6.Pin_0, J2.pin1
  N4: U1.pin4, R9.Pin_0, R10.Pin_0, J3.pin1
  N5: U1.pin5, パーツ1.GND, LED1.cathode, LED2.cathode, LED3.cathode
  N6: パーツ1.A4/SDA, R11.Pin_1, R12.Pin_1
  N7: パーツ1.A5/SCL, R7.Pin_1, R8.Pin_1
  N8: パーツ1.D2, R3.Pin_1, R4.Pin_1
  N9: パーツ1.5V, R4.Pin_0, R8.Pin_0, R12.Pin_0
  N10: R2.Pin_1, R3.Pin_0, LED1.anode
  N11: R6.Pin_1, R7.Pin_0, LED2.anode
  N12: LED3.anode, R10.Pin_1, R11.Pin_0

notes:
  3.3V
  5V
