# Fritzing sketch Arduino-I2C-Level-Shift-LED (saved by Fritzing 0.9.0b)
breadboards: 1

parts:
  U1 = mystery part, 5 pins [chip_label="I2C LCD"]  # not connected
  パーツ1 = Arduino Uno (Rev3)
  R1 = Resistor [tolerance=±5% resistance=10k package=THT]
  R2 = Resistor [tolerance=±5% resistance=330 package=THT]
  LED1 = LED - 5mm [color="Red (633nm)" package="5 mm [THT]"]
  LED2 = LED - 5mm [color="Red (633nm)" package="5 mm [THT]"]
  R3 = Resistor [tolerance=±5% resistance=330 package=THT]
  R4 = Resistor [tolerance=±5% resistance=10k package=THT]
  J1 = female pin header, 1 pin [form="♀ (female)"]
  R6 = Resistor [tolerance=±5% resistance=10k package=THT]
  R7 = Resistor [tolerance=±5% resistance=330 package=THT]
  R8 = Resistor [tolerance=±5% resistance=330 package=THT]
  LED3 = LED - 3mm [color="Blue (525nm)" package="3 mm [THT]"]
  R9 = Resistor [tolerance=±5% resistance=10k package=THT]
  J2 = female pin header, 1 pin [form="♀ (female)"]

nets:
  N1: パーツ1.D2, R8.Pin_1, R9.Pin_1
  N2: パーツ1.D3_PWM, R3.Pin_1, R4.Pin_1
  N3: パーツ1.3V3, R1.Pin_1, R6.Pin_1
  N4: パーツ1.5V, R4.Pin_0, R9.Pin_0
  N5: パーツ1.GND, LED2.cathode, LED3.cathode
  N6: R1.Pin_0, R2.Pin_0, J1.pin1
  N7: R2.Pin_1, LED1.anode, R3.Pin_0
  N8: LED1.cathode, LED2.anode
  N9: R6.Pin_0, R7.Pin_0, J2.pin1
  N10: R7.Pin_1, R8.Pin_0, LED3.anode

notes:
  3.3V
  5V
