# Fritzing sketch Arduino-I2C-Level-Shift-PCA9306-LCD (saved by Fritzing 0.9.0b)
breadboards: 1

parts:
  U1 = mystery part, 5 pins [chip_label="I2C LCD"]
  パーツ1 = Arduino Uno (Rev3)
  U2 = mystery part, 8 pins [chip_label=PCA9306]
  J1 = female pin header, 2 pins [form="♀ (female)"]
  U3 = mystery part, 8 pins [chip_label=PCA9306]
  J4 = female pin header, 1 pin [form="♀ (female)"]

nets:
  N1: U1.pin1, パーツ1.3V3, U2.pin5, U3.pin5
  N2: U1.pin2, U3.pin6, J4.pin1
  N3: U1.pin3, U2.pin6, J1.pin1
  N4: U1.pin4, U2.pin7, J1.pin2
  N5: U1.pin5, パーツ1.GND, U2.pin1, U3.pin1
  N6: パーツ1.A4/SDA, U2.pin2
  N7: パーツ1.A5/SCL, U2.pin3
  N8: パーツ1.D2, U3.pin3
  N9: パーツ1.5V, U2.pin4, U3.pin4

notes:
  3.3V
  5V
