# Fritzing sketch Bunatsu (saved by Fritzing 0.9.0b)
breadboards: 1

parts:
  R1 = Resistor [tolerance=±5% resistance=10k package=THT]
  R2 = Resistor [tolerance=±5% resistance=10k package=THT]
  R3 = Resistor [tolerance=±5% resistance=2k package=THT]
  R4 = Resistor [tolerance=±5% resistance=2k package=THT]
  R5 = Resistor [tolerance=±5% resistance=100 package=THT]
  R6 = Resistor [tolerance=±5% resistance=100 package=THT]
  R7 = Resistor [tolerance=±5% resistance=0.47 package=THT]
  R8 = Resistor [tolerance=±5% resistance=0.47 package=THT]
  J1 = female pin header, 1 pin [form="♀ (female)"]
  J2 = female pin header, 1 pin [form="♀ (female)"]
  J3 = female pin header, 1 pin [form="♀ (female)"]
  J4 = female pin header, 1 pin [form="♀ (female)"]
  J6 = female pin header, 1 pin [form="♀ (female)"]
  J5 = female pin header, 1 pin [form="♀ (female)"]

nets:
  N1: R1.Pin_0, R5.Pin_0, J1.pin1
  N2: R1.Pin_1, R4.Pin_0, J3.pin1
  N3: R2.Pin_0, R6.Pin_0, J2.pin1
  N4: R2.Pin_1, R3.Pin_0, J4.pin1
  N5: R5.Pin_1, R7.Pin_0, J5.pin1
  N6: R6.Pin_1, R8.Pin_0, J6.pin1
  N7: R7.Pin_1, R8.Pin_1

notes:
  Positive
  Negative
