# Fritzing sketch I2C-LCD (saved by Fritzing 0.9.0b)
breadboards: 1

parts:
  U1 = mystery part, 5 pins [chip_label="I2C LCD"]
  U2 = atmega328 [package=dip]
  VCC1 = Battery
  C1 = Ceramic Capacitor [capacitance=100nF package="100 mil [THT, multilayer]"]

nets:
  N1: U1.pin1, U2.VCC, VCC1.+, C1.0
  N2: U1.pin2, U2.A3
  N3: U1.pin3, U2.A5
  N4: U1.pin4, U2.A4
  N5: U1.pin5, U2.GND#7, VCC1.-, C1.1

notes:
  3V
