# Fritzing sketch Integration-Test (saved by Fritzing 0.9.0b)
perfboards: 3
breadboards: 3

parts:
  J1 = female pin header, 1 pin [form="♀ (female)"]
  J2 = female pin header, 1 pin [form="♀ (female)"]
  J3 = female pin header, 1 pin [form="♀ (female)"]
  J4 = female pin header, 1 pin [form="♀ (female)"]
  J5 = female pin header, 1 pin [form="♀ (female)"]
  J6 = female pin header, 1 pin [form="♀ (female)"]
  J7 = female pin header, 1 pin [form="♀ (female)"]
  J8 = female pin header, 1 pin [form="♀ (female)"]
  VCC1 = Battery block 9V
  VCC2 = Battery block 9V
  J9 = female pin header, 3 pins [form="♀ (female)"]
  J10 = female pin header, 3 pins [form="♀ (female)"]
  J11 = female pin header, 3 pins [form="♀ (female)"]
  J12 = female pin header, 3 pins [form="♀ (female)"]
  J13 = female pin header, 4 pins [form="♀ (female)"]
  IC1 = Dual Op-Amp [package=dip08]
  R1 = Resistor [tolerance=±5% resistance=220 package=THT]
  R2 = Resistor [tolerance=±5% resistance=220 package=THT]
  R3 = Resistor [tolerance=±5% resistance=0.47 package=THT]
  R4 = Resistor [tolerance=±5% resistance=0.47 package=THT]
  R5 = Resistor [tolerance=±5% resistance=10k package=THT]
  R6 = Resistor [tolerance=±5% resistance=10k package=THT]
  R7 = Resistor [tolerance=±5% resistance=2k package=THT]
  R8 = Resistor [tolerance=±5% resistance=2k package=THT]
  R9 = Resistor [tolerance=±5% resistance=10k package=THT]
  R10 = Resistor [tolerance=±5% resistance=2k package=THT]
  R11 = Resistor [tolerance=±5% resistance=10k package=THT]
  R12 = Resistor [tolerance=±5% resistance=2k package=THT]
  C1 = Ceramic Capacitor [capacitance=100nF package="100 mil [THT, multilayer]"]
  C2 = Ceramic Capacitor [capacitance=100nF package="100 mil [THT, multilayer]"]

nets:
  N1: J1.pin1, VCC1.+, J9.pin1
  N2: J2.pin1, J3.pin1, VCC1.-, VCC2.+, J9.pin2
  N3: J4.pin1, VCC2.-, J9.pin3
  N4: J5.pin1, R1.Pin_0, R5.Pin_0
  N5: J6.pin1, J7.pin1
  N6: J8.pin1, R2.Pin_1, R6.Pin_0
  N7: J10.pin1, J12.pin1
  N8: J10.pin2, J12.pin2
  N9: J10.pin3, J12.pin3
  N10: J11.pin1, IC1.A_V-, C1.0
  N11: J11.pin3, IC1.A_V+, C2.0
  N12: J13.pin1, R5.Pin_1, R7.Pin_0
  N13: J13.pin2, IC1.B_OUT, R11.Pin_0
  N14: J13.pin3, R6.Pin_1, R8.Pin_0
  N15: J13.pin4, IC1.A_-IN, R9.Pin_1, R10.Pin_0
  N16: IC1.A_OUT, R9.Pin_0
  N17: IC1.A_+IN, R1.Pin_1, R3.Pin_0
  N18: IC1.B_+IN, R2.Pin_0, R4.Pin_1
  N19: IC1.B_-IN, R11.Pin_1, R12.Pin_1
  N20: R3.Pin_1, R4.Pin_0, R7.Pin_1, R8.Pin_1, R10.Pin_1, R12.Pin_0, C1.1, C2.1

notes:
  +15V
  -15V
  Dual Power Supply
  Meas Power Supply
  Digital Part
  Load
  Current
  Detection
  Meas-
  Meas+
