# Fritzing sketch SPLC792-I2C-2 (saved by Fritzing 0.9.0b)
breadboards: 1

parts:
  U1 = mystery part, 7 pins [chip_label=SPLC792-I2C]
  U2 = atmega328 [package=dip]
  C1 = Ceramic Capacitor [capacitance=100nF package="100 mil [THT, multilayer]"]
  VCC1 = Battery
  VCC2 = 4 x AAA Battery Mount

nets:
  N1: U1.pin1, U2.D2
  N2: U1.pin2, U2.A5
  N3: U1.pin3, U2.A4
  N4: U1.pin4, U2.GND#7, C1.1, VCC1.-, VCC2.-
  N5: U1.pin7, VCC1.+
  N6: U2.VCC, C1.0, VCC2.+

notes:
  +3.3V
  +5V
