# Fritzing sketch SPLC792-I2C-ADC (saved by Fritzing 0.9.0b)
breadboards: 1

parts:
  U1 = mystery part, 7 pins [chip_label=SPLC792-I2C]
  U2 = atmega328 [package=dip]
  C1 = Ceramic Capacitor [capacitance=100nF package="100 mil [THT, multilayer]"]
  VCC1 = Battery
  VCC2 = 4 x AAA Battery Mount
  C2 = Ceramic Capacitor [capacitance=100nF package="100 mil [THT, multilayer]"]
  C3 = Ceramic Capacitor [capacitance=100nF package="100 mil [THT, multilayer]"]
  L1 = Inductor [package="400 mil [THT]"]
  J1 = female pin header, 4 pins [form="♀ (female)"]

nets:
  N1: U1.pin1, U2.D2
  N2: U1.pin2, U2.A5
  N3: U1.pin3, U2.A4
  N4: U1.pin4, U2.GND, C1.1, VCC1.-, VCC2.-, C2.0, C3.1
  N5: U1.pin7, VCC1.+
  N6: U2.VCC, C1.0, VCC2.+, L1.pin_1
  N7: U2.AVCC, C3.0, L1.pin_0
  N8: U2.AREF, C2.1
  N9: U2.A0, J1.pin4
  N10: U2.A1, J1.pin3
  N11: U2.A2, J1.pin2
  N12: U2.A3, J1.pin1

notes:
  +3.3V
  +5V
