# Fritzing sketch Shunt-Regurator (saved by Fritzing 0.9.0b)
breadboards: 1

parts:
  R14 = Resistor [tolerance=±5% resistance=330 package=THT]
  U1 = mystery part, 3 pins [chip_label=TL431]
  VCC1 = 4 x AAA Battery Mount
  J1 = female pin header, 1 pin [form="♀ (female)"]

nets:
  N1: R14.Pin_0, U1.pin1, U1.pin3, J1.pin1
  N2: U1.pin2, VCC1.-
