# Fritzing sketch TLV1117 (saved by Fritzing 0.9.0b)
breadboards: 1

parts:
  C1 = Electrolytic Capacitor [capacitance=10µF voltage=20V package="100 mil [THT, electrolytic]"]
  C2 = Electrolytic Capacitor [capacitance=0.1mF voltage=20V package="200 mil [THT, electrolytic]"]
  D1 = Rectifier Diode [part_number=1N4001 package="300 mil [THT]"]
  VCC1 = Battery block 9V
  R1 = Resistor [tolerance=±5% resistance=220 package=THT]
  J1 = female pin header, 1 pin [form="♀ (female)"]
  U1 = mystery part, 5 pins [chip_label=TL:V1117]

nets:
  N1: C1.-, C2.-, VCC1.-, R1.Pin_0, U1.pin1
  N2: C1.+, D1.cathode, VCC1.+, U1.pin5
  N3: C2.+, D1.anode, R1.Pin_1, J1.pin1, U1.pin3
