# Fritzing sketch VAMeter-Partial-VRegulator (saved by Fritzing 0.9.0b)
breadboards: 1

parts:
  R1 = Resistor [tolerance=±5% resistance=10k package=THT]
  R2 = Resistor [tolerance=±5% resistance=10k package=THT]
  R5 = Resistor [tolerance=±5% resistance=10k package=THT]
  R6 = Resistor [tolerance=±5% resistance=10k package=THT]
  R7 = Resistor [tolerance=±5% resistance=10k package=THT]
  R8 = Resistor [tolerance=±5% resistance=10k package=THT]
  J1 = female pin header, 1 pin [form="♀ (female)"]
  VCC1 = Battery block 9V
  VCC2 = Battery block 9V
  R3 = Resistor [tolerance=±5% resistance=10k package=THT]
  R4 = Resistor [tolerance=±5% resistance=10k package=THT]
  R12 = TRIMPOT [package=trimpot_pth_s3_lock]
  R13 = TRIMPOT [package=trimpot_pth_s3_lock]
  U1 = mystery part, 3 pins [chip_label=TL431]
  R14 = Resistor [tolerance=±5% resistance=330 package=THT]
  J3 = female pin header, 1 pin [form="♀ (female)"]
  C1 = Electrolytic Capacitor [capacitance=10µF package="100 mil [THT, electrolytic]"]
  C2 = Electrolytic Capacitor [capacitance=0.1mF voltage=16V package="200 mil [THT, electrolytic]"]
  R15 = Resistor [tolerance=±5% resistance=220 package=THT]
  J4 = female pin header, 1 pin [form="♀ (female)"]
  D1 = Rectifier Diode [part_number=1N4001 package="300 mil [THT]"]  # not connected
  U2 = mystery part, 5 pins [chip_label=TLV1117]
  J5 = female pin header, 1 pin [form="♀ (female)"]

nets:
  N1: R1.Pin_0, R12.WIPER, C1.+, U2.pin5
  N2: R1.Pin_1, R2.Pin_0
  N3: R2.Pin_1, R4.Pin_0
  N4: R5.Pin_0, VCC1.-, VCC2.+, R3.Pin_1, R12.CCW, R13.CCW, U1.pin1, U1.pin3
  N5: R5.Pin_1, R6.Pin_0, J3.pin1
  N6: R6.Pin_1, R7.Pin_0
  N7: R7.Pin_1, R8.Pin_0
  N8: R8.Pin_1, R13.WIPER, R14.Pin_1
  N9: J1.pin1, R3.Pin_0, R4.Pin_1
  N10: VCC1.+, R12.CW
  N11: VCC2.-, R13.CW
  N12: U1.pin2, R14.Pin_0, C1.-, C2.-, R15.Pin_0, U2.pin1, J5.pin1
  N13: C2.+, R15.Pin_1, J4.pin1, U2.pin3

notes:
  正電源
  負電源
  負荷抵抗
