# Fritzing sketch VAMeter-VoltageFollower (saved by Fritzing 0.9.0b)
breadboards: 1

parts:
  R1 = Resistor [tolerance=±5% resistance=10k package=THT]
  R2 = Resistor [tolerance=±5% resistance=10k package=THT]
  R5 = Resistor [tolerance=±5% resistance=10k package=THT]
  R6 = Resistor [tolerance=±5% resistance=10k package=THT]
  R7 = Resistor [tolerance=±5% resistance=10k package=THT]
  R8 = Resistor [tolerance=±5% resistance=10k package=THT]
  J1 = female pin header, 1 pin [form="♀ (female)"]
  VCC1 = Battery block 9V
  VCC2 = Battery block 9V
  R3 = Resistor [tolerance=±5% resistance=10k package=THT]
  R4 = Resistor [tolerance=±5% resistance=10k package=THT]
  IC1 = Dual Op-Amp [package=dip08]
  C1 = Ceramic Capacitor [capacitance=100nF package="100 mil [THT, multilayer]"]
  C2 = Ceramic Capacitor [capacitance=100nF package="100 mil [THT, multilayer]"]
  R9 = Resistor [tolerance=±5% resistance=100k package=THT]
  R10 = Resistor [tolerance=±5% resistance=100k package=THT]
  J2 = female pin header, 1 pin [form="♀ (female)"]
  R11 = Resistor [tolerance=±5% resistance=47k package=THT]
  R12 = TRIMPOT [package=trimpot_pth_s3_lock]
  R13 = TRIMPOT [package=trimpot_pth_s3_lock]

nets:
  N1: R1.Pin_0, IC1.A_V+, C1.1, R12.WIPER
  N2: R1.Pin_1, R2.Pin_0
  N3: R2.Pin_1, R4.Pin_0
  N4: R5.Pin_0, VCC1.-, VCC2.+, R3.Pin_1, C1.0, C2.1, R11.Pin_0, R12.CCW, R13.CCW
  N5: R5.Pin_1, R6.Pin_0, IC1.A_+IN
  N6: R6.Pin_1, R7.Pin_0
  N7: R7.Pin_1, R8.Pin_0
  N8: R8.Pin_1, IC1.A_V-, C2.0, R13.WIPER
  N9: J1.pin1, R3.Pin_0, R4.Pin_1
  N10: VCC1.+, R12.CW
  N11: VCC2.-, R13.CW
  N12: IC1.A_OUT, IC1.A_-IN, R10.Pin_1
  N13: IC1.B_+IN, R11.Pin_1
  N14: IC1.B_-IN, R9.Pin_1, R10.Pin_0
  N15: IC1.B_OUT, R9.Pin_0, J2.pin1

notes:
  正電源
  負電源
