# Fritzing sketch Variable_Power_Supply (saved by Fritzing 0.9.0b)
breadboards: 3

parts:
  U1 = atmega328 [package=dip]
  R6 = Resistor [tolerance=±1% resistance=10k package=THT]
  R14 = Resistor [tolerance=±5% resistance=0.47 package=THT]
  R16 = Resistor [tolerance=±1% resistance=10k package=THT]
  R17 = Resistor [tolerance=±1% resistance=10k package=THT]
  R18 = Resistor [tolerance=±1% resistance=10k package=THT]
  R19 = Resistor [tolerance=±1% resistance=10k package=THT]
  R20 = Resistor [tolerance=±1% resistance=10k package=THT]
  R21 = Resistor [tolerance=±1% resistance=10k package=THT]
  R22 = Resistor [tolerance=±1% resistance=10k package=THT]
  R23 = Resistor [tolerance=±5% resistance=0.47 package=THT]
  LED1 = LED - 3mm [color="Blue (505nm)" package="3 mm [THT]"]
  R24 = Resistor [tolerance=±5% resistance=1k package=THT]
  VCC1 = 4 x AAA Battery Mount
  L1 = Inductor [package="400 mil [THT]"]
  C1 = Ceramic Capacitor [capacitance=100nF package="100 mil [THT, multilayer]"]
  C2 = Ceramic Capacitor [capacitance=100nF package="100 mil [THT, multilayer]"]
  VCC2 = Battery block 9V
  VCC3 = Battery block 9V
  R25 = TRIMPOT [package=3386u]
  R26 = TRIMPOT [package=3386u]
  R27 = Resistor [tolerance=±5% resistance=470 package=THT]
  R28 = Resistor [tolerance=±5% resistance=470 package=THT]
  LCD1 = LCD screen
  R29 = TRIMPOT [package=trimpot_pth_s3_lock]
  IC1 = Dual Op-Amp [package=dip08]
  R30 = Resistor [tolerance=±5% resistance=10k package=THT]
  R31 = Resistor [tolerance=±5% resistance=10k package=THT]
  R32 = Resistor [tolerance=±5% resistance=4.7k package=THT]

nets:
  N1: U1.D0_(RX), LCD1.DB4
  N2: U1.D1_(TX), LCD1.DB5
  N3: U1.D2, LCD1.DB6
  N4: U1.D3_(PWM), LCD1.DB7
  VCC: U1.VCC, L1.pin_0, C1.0, LCD1.VDD, LCD1.LED+, R29.CCW
  N5: U1.GND, R14.Pin_1, R18.Pin_1, R22.Pin_1, R23.Pin_1, LED1.cathode, VCC1.-, C1.1, C2.0, VCC2.-, VCC3.+, R25.CW, R26.CW, LCD1.R/W, LCD1.LED-, R29.CW, IC1.B_+IN, R32.Pin_1
  N6: U1.D5_(PWM), LCD1.RS
  N7: U1.D6_(PWM), LCD1.E
  N8: U1.AVCC, R24.Pin_1, VCC1.+, L1.pin_1, C2.1
  N9: U1.AREF, LED1.anode, R24.Pin_0
  N10: U1.A0, R14.Pin_0, R27.Pin_1
  N11: U1.A1, R17.Pin_1, R18.Pin_0
  N12: U1.A2, R23.Pin_0, R28.Pin_0
  N13: U1.A3, IC1.A_OUT, R30.Pin_0
  N14: R6.Pin_0, R26.WIPER, R27.Pin_0
  N15: R6.Pin_1, R16.Pin_0, IC1.A_V+
  N16: R16.Pin_1, R17.Pin_0
  N17: R19.Pin_0, R25.WIPER, R28.Pin_1, IC1.A_V-
  N18: R19.Pin_1, R20.Pin_0
  N19: R20.Pin_1, R21.Pin_0
  N20: R21.Pin_1, R22.Pin_0, R31.Pin_1
  N21: VCC2.+, R26.CCW
  N22: VCC3.-, R25.CCW
  N23: LCD1.V0, R29.WIPER
  N24: IC1.A_-IN, R30.Pin_1, R31.Pin_0
  N25: IC1.A_+IN, R32.Pin_0
  N26: IC1.B_-IN, IC1.B_OUT

notes:
  Analog Pwr
  Digital Pwr
  5V
  負電源
  正電源
