# Fritzing sketch inverting amplifier (saved by Fritzing 0.9.0b)
breadboards: 1

parts:
  IC1 = Dual Op-Amp [package=dip08]
  R1 = Resistor [tolerance=±5% resistance=10k package=THT]
  J1 = female pin header, 1 pin [form="♀ (female)"]
  R3 = Resistor [tolerance=±5% resistance=47k package=THT]  # not connected
  R4 = Resistor [tolerance=±5% resistance=10k package=THT]
  J2 = female pin header, 1 pin [form="♀ (female)"]
  R5 = Resistor [tolerance=±5% resistance=10k package=THT]
  R6 = Resistor [tolerance=±5% resistance=10k package=THT]
  R7 = Resistor [tolerance=±5% resistance=47k package=THT]
  J3 = female pin header, 1 pin [form="♀ (female)"]
  J4 = female pin header, 1 pin [form="♀ (female)"]

nets:
  N1: IC1.A_OUT, R1.Pin_0, J2.pin1
  N2: IC1.A_-IN, R1.Pin_1, R4.Pin_0
  N3: IC1.B_+IN, R7.Pin_0
  N4: IC1.B_-IN, R5.Pin_1, R6.Pin_0
  N5: IC1.B_OUT, R5.Pin_0, J3.pin1
  N6: J1.pin1, R4.Pin_1
  N7: R6.Pin_1, J4.pin1
