# Fritzing sketch 反転アンプ (saved by Fritzing 0.9.0b)
breadboards: 1

parts:
  R1 = Resistor [tolerance=±5% resistance=10k package=THT]
  R2 = Resistor [tolerance=±5% resistance=10k package=THT]
  R3 = Resistor [tolerance=±5% resistance=10k package=THT]
  R4 = Resistor [tolerance=±5% resistance=10k package=THT]
  R5 = Resistor [tolerance=±5% resistance=10k package=THT]
  R6 = Resistor [tolerance=±5% resistance=10k package=THT]
  R7 = Resistor [tolerance=±5% resistance=10k package=THT]
  R8 = Resistor [tolerance=±5% resistance=10k package=THT]
  VCC2 = Battery block 9V
  VCC1 = Battery block 9V
  IC1 = Dual Op-Amp [package=dip08]
  R9 = Resistor [tolerance=±5% resistance=10k package=THT]
  R10 = Resistor [tolerance=±5% resistance=47k package=THT]
  R11 = Resistor [tolerance=±5% resistance=10k package=THT]
  U1 = Header 1 [package=1x01_offset]
  U2 = Header 1 [package=1x01_offset]

nets:
  N1: R1.Pin_0, R5.Pin_0, VCC2.-, VCC1.+, R10.Pin_0
  N2: R1.Pin_1, R2.Pin_0
  N3: R2.Pin_1, R3.Pin_0
  N4: R3.Pin_1, R4.Pin_0, U1.1
  N5: R4.Pin_1, VCC2.+, IC1.A_V+, R11.Pin_0
  N6: R5.Pin_1, R6.Pin_0
  N7: R6.Pin_1, R7.Pin_0
  N8: R7.Pin_1, R8.Pin_0, IC1.A_+IN
  N9: R8.Pin_1, VCC1.-, IC1.A_V-
  N10: IC1.A_OUT, IC1.A_-IN, R9.Pin_0
  N11: IC1.B_+IN, R10.Pin_1, R11.Pin_1
  N12: IC1.B_-IN, R9.Pin_1
  N13: IC1.B_OUT, U2.1

notes:
  負電源
  正電源
